// Logisim project YnZn-or-YZ.circ as structural Verilog: 1 circuit, main circuit main
module main (
  input  Y,
  input  Z,
  output Y_prime_Z_prime_YZ
);

  wire and_1_out, and_2_out, not_1_out, not_2_out;

  and and_1 (and_1_out, Z, Y);
  not not_1 (not_1_out, Y);
  and and_2 (and_2_out, not_1_out, not_2_out);
  not not_2 (not_2_out, Z);
  or or_1 (Y_prime_Z_prime_YZ, and_1_out, and_2_out);

  // Notes on the sheet:
  //   YZ
  //   Y'Z'
endmodule
