// Logisim project ALU-components.circ as structural Verilog: 7 circuits, main circuit main
module main (
  input  in_1,
  input  in_2,
  output out_3,
  output out_4
);

  HalfAdder halfadder_1 (.Input_X(in_1), .Input_Y(in_2), .Sum(out_3), .Carry(out_4));
endmodule

module HalfAdder (
  input  Input_X,
  input  Input_Y,
  output Sum,
  output Carry
);

  xor xor_1 (Sum, Input_X, Input_Y);
  and and_1 (Carry, Input_X, Input_Y);
endmodule

module FullAdder (
  input  Input_C,
  input  Input_X,
  input  Input_Y,
  output Sum,
  output Carry
);

  wire halfadder_1_carry, halfadder_1_sum, halfadder_2_carry;

  HalfAdder halfadder_1 (.Input_X(Input_X), .Input_Y(Input_Y), .Sum(halfadder_1_sum), .Carry(halfadder_1_carry));
  HalfAdder halfadder_2 (.Input_X(halfadder_1_sum), .Input_Y(Input_C), .Sum(Sum), .Carry(halfadder_2_carry));
  or or_1 (Carry, halfadder_2_carry, halfadder_1_carry);
endmodule

module FourBitAdderSubtractor (
  input  Flag,
  input  X0,
  input  Y0,
  input  X1,
  input  Y1,
  input  X2,
  input  Y2,
  input  X3,
  input  Y3,
  output S0,
  output S1,
  output S2,
  output S3
);

  wire fulladder_1_carry, fulladder_2_carry, fulladder_3_carry, xor_1_out, xor_2_out, xor_3_out, xor_4_out;

  xor xor_1 (xor_1_out, Flag, Y0);
  xor xor_2 (xor_2_out, Flag, Y1);
  xor xor_3 (xor_3_out, Flag, Y2);
  xor xor_4 (xor_4_out, Flag, Y3);
  FullAdder fulladder_1 (.Input_C(Flag), .Input_X(X0), .Input_Y(xor_1_out), .Sum(S0), .Carry(fulladder_1_carry));
  FullAdder fulladder_2 (
    .Input_C(fulladder_1_carry), .Input_X(X1), .Input_Y(xor_2_out), .Sum(S1), .Carry(fulladder_2_carry));
  FullAdder fulladder_3 (
    .Input_C(fulladder_2_carry), .Input_X(X2), .Input_Y(xor_3_out), .Sum(S2), .Carry(fulladder_3_carry));
  FullAdder fulladder_4 (.Input_C(fulladder_3_carry), .Input_X(X3), .Input_Y(xor_4_out), .Sum(S3));  // open: Carry

  // Notes on the sheet:
  //   If (flag == 0), then S = X + Y --> Addition
  //   If (flag == 1), then S = X + Y' + 1 --> Subtraction
endmodule

module Inverter (
  input  Flag,
  input  Input,
  output out_3
);

  xor xor_1 (out_3, Flag, Input);
endmodule

module Decoder (
  input  [1:0] in_1,
  output O0,
  output O1,
  output O2,
  output O3
);

  wire not_1_out, not_2_out;

  not not_1 (not_1_out, in_1[0]);
  not not_2 (not_2_out, in_1[1]);
  and u_O0 (O0, not_1_out, not_2_out);
  and u_O1 (O1, in_1[0], not_2_out);
  and u_O2 (O2, not_1_out, in_1[1]);
  and u_O3 (O3, in_1[0], in_1[1]);
endmodule

module Multiplexer (
  input  [7:0] in_1,
  input  [7:0] in_2,
  input  [7:0] in_3,
  input  [7:0] in_4,
  input  [1:0] SelectBits,
  output [7:0] out_6
);

  wire [7:0] multiplexer_1_out, multiplexer_2_out;

  Multiplexer_part #(.width(8), .disabled(0), .enable("false")) multiplexer_1 (
    .in0(in_1), .in1(in_2), .out(multiplexer_1_out), .sel(SelectBits[0]));
  Multiplexer_part #(.width(8), .disabled(0), .enable("false")) multiplexer_2 (
    .in0(in_3), .in1(in_4), .out(multiplexer_2_out), .sel(SelectBits[0]));
  Multiplexer_part #(.width(8), .disabled(0), .enable("false")) multiplexer_3 (
    .in0(multiplexer_1_out), .in1(multiplexer_2_out), .out(out_6), .sel(SelectBits[1]));

  // Notes on the sheet:
  //   Implement 4-->1 multiplexer using 2-->1 multiplexers
endmodule
