// Logisim project assignment12-Hinke.circ as structural Verilog: 8 circuits, main circuit main
module main (
  input  in_1,
  input  in_2,
  output out_3,
  output out_4
);

  HalfAdder halfadder_1 (.Input_X(in_1), .Input_Y(in_2), .Sum(out_3), .Carry(out_4));
endmodule

module HalfAdder (
  input  Input_X,
  input  Input_Y,
  output Sum,
  output Carry
);

  xor xor_1 (Sum, Input_X, Input_Y);
  and and_1 (Carry, Input_X, Input_Y);
endmodule

module FullAdder (
  input  Input_C,
  input  Input_X,
  input  Input_Y,
  output Sum,
  output Carry
);

  wire HalfAdder_2_carry, HalfAdder_carry, HalfAdder_sum;

  HalfAdder HalfAdder (.Input_X(Input_X), .Input_Y(Input_Y), .Sum(HalfAdder_sum), .Carry(HalfAdder_carry));
  HalfAdder HalfAdder_2 (.Input_X(HalfAdder_sum), .Input_Y(Input_C), .Sum(Sum), .Carry(HalfAdder_2_carry));
  or or_1 (Carry, HalfAdder_2_carry, HalfAdder_carry);
endmodule

module Pr1_EightBitAdderSubtractor (
  input  Flag,
  input  X0,
  input  Y0,
  input  X1,
  input  Y1,
  input  X2,
  input  Y2,
  input  X3,
  input  Y3,
  input  X4,
  input  Y4,
  input  X5,
  input  Y5,
  input  X6,
  input  Y6,
  input  X7,
  input  Y7,
  output S0,
  output S1,
  output S2,
  output S3,
  output S4,
  output S5,
  output S6,
  output S7
);

  wire FullAdder_2_carry, FullAdder_3_carry, FullAdder_4_carry, FullAdder_5_carry, FullAdder_6_carry,
       FullAdder_7_carry, FullAdder_carry, xor_1_out, xor_2_out, xor_3_out, xor_4_out, xor_5_out, xor_6_out,
       xor_7_out, xor_8_out;

  xor xor_1 (xor_1_out, Flag, Y0);
  xor xor_2 (xor_2_out, Flag, Y1);
  xor xor_3 (xor_3_out, Flag, Y2);
  xor xor_4 (xor_4_out, Flag, Y3);
  xor xor_5 (xor_5_out, Flag, Y4);
  xor xor_6 (xor_6_out, Flag, Y5);
  xor xor_7 (xor_7_out, Flag, Y6);
  xor xor_8 (xor_8_out, Flag, Y7);
  FullAdder FullAdder (.Input_C(Flag), .Input_X(X0), .Input_Y(xor_1_out), .Sum(S0), .Carry(FullAdder_carry));
  FullAdder FullAdder_2 (
    .Input_C(FullAdder_carry), .Input_X(X1), .Input_Y(xor_2_out), .Sum(S1), .Carry(FullAdder_2_carry));
  FullAdder FullAdder_3 (
    .Input_C(FullAdder_2_carry), .Input_X(X2), .Input_Y(xor_3_out), .Sum(S2), .Carry(FullAdder_3_carry));
  FullAdder FullAdder_4 (
    .Input_C(FullAdder_3_carry), .Input_X(X3), .Input_Y(xor_4_out), .Sum(S3), .Carry(FullAdder_4_carry));
  FullAdder FullAdder_5 (
    .Input_C(FullAdder_4_carry), .Input_X(X4), .Input_Y(xor_5_out), .Sum(S4), .Carry(FullAdder_5_carry));
  FullAdder FullAdder_6 (
    .Input_C(FullAdder_5_carry), .Input_X(X5), .Input_Y(xor_6_out), .Sum(S5), .Carry(FullAdder_6_carry));
  FullAdder FullAdder_7 (
    .Input_C(FullAdder_6_carry), .Input_X(X6), .Input_Y(xor_7_out), .Sum(S6), .Carry(FullAdder_7_carry));
  FullAdder FullAdder_8 (.Input_C(FullAdder_7_carry), .Input_X(X7), .Input_Y(xor_8_out), .Sum(S7));  // open: Carry

  // Notes on the sheet:
  //   If (flag == 0), then S = X + Y --> Addition
  //   If (flag == 1), then S = X + Y' + 1 --> Subtraction
endmodule

module Pr3_4to1Multiplexer (
  input  [7:0] in_1,
  input  [7:0] in_2,
  input  [7:0] in_3,
  input  [7:0] in_4,
  input  [1:0] SelectBits,
  output [7:0] out_6
);

  wire [7:0] multiplexer_1_out, multiplexer_2_out;

  Multiplexer #(.width(8), .disabled(0), .enable("false")) multiplexer_1 (
    .in0(in_1), .in1(in_2), .out(multiplexer_1_out), .sel(SelectBits[0]));
  Multiplexer #(.width(8), .disabled(0), .enable("false")) multiplexer_2 (
    .in0(in_3), .in1(in_4), .out(multiplexer_2_out), .sel(SelectBits[0]));
  Multiplexer #(.width(8), .disabled(0), .enable("false")) multiplexer_3 (
    .in0(multiplexer_1_out), .in1(multiplexer_2_out), .out(out_6), .sel(SelectBits[1]));

  // Notes on the sheet:
  //   Implement 4-->1 multiplexer using 2-->1 multiplexers
endmodule

module Pr4_16to1Multiplexer (
  input  [7:0] in_1,
  input  [7:0] in_2,
  input  [7:0] in_3,
  input  [7:0] in_4,
  input  [7:0] in_5,
  input  [7:0] in_6,
  input  [7:0] in_7,
  input  [7:0] in_8,
  input  [7:0] in_9,
  input  [7:0] in_10,
  input  [7:0] in_11,
  input  [7:0] in_12,
  input  [7:0] in_13,
  input  [7:0] in_14,
  input  [7:0] in_15,
  input  [7:0] in_16,
  input  [3:0] SelectBits,
  output [7:0] out_18
);

  wire [7:0] multiplexer_1_out, multiplexer_2_out, multiplexer_3_out, multiplexer_4_out;

  Multiplexer #(.select(2), .width(8), .disabled(0), .enable("false")) multiplexer_1 (
    .in0(in_1), .in1(in_2), .in2(in_3), .in3(in_4), .out(multiplexer_1_out), .sel(SelectBits[1:0]));
  Multiplexer #(.select(2), .width(8), .disabled(0), .enable("false")) multiplexer_2 (
    .in0(in_5), .in1(in_6), .in2(in_7), .in3(in_8), .out(multiplexer_2_out), .sel(SelectBits[1:0]));
  Multiplexer #(.select(2), .width(8), .disabled(0), .enable("false")) multiplexer_3 (
    .in0(in_9), .in1(in_10), .in2(in_11), .in3(in_12), .out(multiplexer_3_out), .sel(SelectBits[1:0]));
  Multiplexer #(.select(2), .width(8), .disabled(0), .enable("false")) multiplexer_4 (
    .in0(in_13), .in1(in_14), .in2(in_15), .in3(in_16), .out(multiplexer_4_out), .sel(SelectBits[1:0]));
  Multiplexer #(.select(2), .width(8), .disabled(0), .enable("false")) multiplexer_5 (
    .in0(multiplexer_1_out), .in1(multiplexer_2_out), .in2(multiplexer_3_out), .in3(multiplexer_4_out),
    .out(out_18), .sel(SelectBits[3:2]));

  // Notes on the sheet:
  //   Implement 16-->1 multiplexer using combination of 4-->1 and 2-->1 multiplexers
endmodule

module Pr2_FullAdderDecoder (
  input  Input_C,
  input  Input_A,
  input  Input_B,
  output Sum,
  output Carry
);

  wire decoder_1_out1, decoder_1_out2, decoder_1_out3, decoder_1_out4, decoder_1_out5, decoder_1_out6,
       decoder_1_out7;

  Decoder #(.select(3), .disabled(0), .enable("false")) decoder_1 (
    .out1(decoder_1_out1), .out2(decoder_1_out2), .out3(decoder_1_out3), .out4(decoder_1_out4),
    .out5(decoder_1_out5), .out6(decoder_1_out6), .out7(decoder_1_out7), .sel({Input_C, Input_B, Input_A}));  // open: out0
  or or_1 (Sum, decoder_1_out1, decoder_1_out2, decoder_1_out4, decoder_1_out7);
  or or_2 (Carry, decoder_1_out3, decoder_1_out5, decoder_1_out6, decoder_1_out7);
endmodule

module Pr2_FourBitAdderSubtractorDecoder (
  input  Flag,
  input  X0,
  input  Y0,
  input  X1,
  input  Y1,
  input  X2,
  input  Y2,
  input  X3,
  input  Y3,
  output S0,
  output S1,
  output S2,
  output S3
);

  wire FullAdderDecoder_2_carry, FullAdderDecoder_3_carry, FullAdderDecoder_carry, xor_1_out, xor_2_out,
       xor_3_out, xor_4_out;

  xor xor_1 (xor_1_out, Flag, Y0);
  xor xor_2 (xor_2_out, Flag, Y1);
  xor xor_3 (xor_3_out, Flag, Y2);
  xor xor_4 (xor_4_out, Flag, Y3);
  Pr2_FullAdderDecoder FullAdderDecoder (
    .Input_C(Flag), .Input_A(X0), .Input_B(xor_1_out), .Sum(S0), .Carry(FullAdderDecoder_carry));
  Pr2_FullAdderDecoder FullAdderDecoder_2 (
    .Input_C(FullAdderDecoder_carry), .Input_A(X1), .Input_B(xor_2_out), .Sum(S1),
    .Carry(FullAdderDecoder_2_carry));
  Pr2_FullAdderDecoder FullAdderDecoder_3 (
    .Input_C(FullAdderDecoder_2_carry), .Input_A(X2), .Input_B(xor_3_out), .Sum(S2),
    .Carry(FullAdderDecoder_3_carry));
  Pr2_FullAdderDecoder FullAdderDecoder_4 (
    .Input_C(FullAdderDecoder_3_carry), .Input_A(X3), .Input_B(xor_4_out), .Sum(S3));  // open: Carry

  // Notes on the sheet:
  //   If (flag == 0), then S = A + B --> Addition
  //   If (flag == 1), then S = A + B' + 1 --> Subtraction
endmodule
