// Logisim project assignment13-Hinke.circ as structural Verilog: 4 circuits, main circuit Pr1-mod4
module Pr1_mod4 (
  output Q1,
  output Q0
);

  wire BlackBoxMod4_q0new, BlackBoxMod4_q1new, clock_1_out;

  Clock clock_1 (.out(clock_1_out));
  BlackBoxMod4 BlackBoxMod4 (.Q0(Q0), .Q1(Q1), .C(clock_1_out), .Q0new(BlackBoxMod4_q0new), .Q1new(BlackBoxMod4_q1new));
  D_Flip_Flop u_Q0 (.clk(clock_1_out), .D(BlackBoxMod4_q0new), .Q(Q0));  // open: Qn, preset, en, reset
  D_Flip_Flop u_Q1 (.clk(clock_1_out), .D(BlackBoxMod4_q1new), .Q(Q1));  // open: Qn, preset, en, reset
endmodule

module Pr2_mod6 (
  output Q2,
  output Q1,
  output Q0
);

  wire BlackBoxMod6_q0new, BlackBoxMod6_q1new, BlackBoxMod6_q2new, clock_1_out;

  Clock clock_1 (.out(clock_1_out));
  BlackBoxMod6 BlackBoxMod6 (
    .Q0(Q0), .Q1(Q1), .Q2(Q2), .Q0new(BlackBoxMod6_q0new), .Q1new(BlackBoxMod6_q1new),
    .Q2new(BlackBoxMod6_q2new));
  D_Flip_Flop u_Q0 (.clk(clock_1_out), .D(BlackBoxMod6_q0new), .Q(Q0));  // open: Qn, preset, en, reset
  D_Flip_Flop u_Q1 (.clk(clock_1_out), .D(BlackBoxMod6_q1new), .Q(Q1));  // open: Qn, preset, en, reset
  D_Flip_Flop u_Q2 (.clk(clock_1_out), .D(BlackBoxMod6_q2new), .Q(Q2));  // open: Qn, preset, en, reset
endmodule

module BlackBoxMod4 (
  input  Q0,
  input  Q1,
  input  C,
  output Q0new,
  output Q1new
);

  wire and_1_out, and_2_out, and_3_out, and_4_out, and_5_out, not_1_out, not_2_out, not_3_out, not_4_out;

  not not_1 (not_1_out, Q0);
  not not_2 (not_2_out, C);
  not not_3 (not_3_out, Q1);
  not not_4 (not_4_out, not_2_out);
  and and_1 (and_1_out, Q0, not_4_out);
  and and_2 (and_2_out, not_1_out, not_2_out);
  and and_3 (and_3_out, Q0, not_3_out);
  and and_4 (and_4_out, Q0, not_4_out);
  and and_5 (and_5_out, not_1_out, Q1, not_2_out);
  or or_1 (Q0new, and_1_out, and_2_out);
  or or_2 (Q1new, and_3_out, and_4_out, and_5_out);
endmodule

module BlackBoxMod6 (
  input  Q0,
  input  Q1,
  input  Q2,
  output Q0new,
  output Q1new,
  output Q2new
);

  ROM #(.addrWidth(3), .dataWidth(3)) rom_1 (.addr({Q2, Q1, Q0}), .data({Q2new, Q1new, Q0new}));  // open: sel

  // Notes on the sheet:
  //   contents of rom_1 (hex, n*v repeats v):
  //   1 2 3 4 5
endmodule
