// Logisim project mod4-counter-ROM-simplified.circ as structural Verilog: 2 circuits, main circuit main
module main (
  output Q1,
  output Q0
);

  wire blackboxromsimplified_1_q0new, blackboxromsimplified_1_q1new, clock_1_out;

  Clock clock_1 (.out(clock_1_out));
  BlackBoxRomSimplified blackboxromsimplified_1 (
    .Q0(Q0), .Q1(Q1), .Q0new(blackboxromsimplified_1_q0new), .Q1new(blackboxromsimplified_1_q1new));
  D_Flip_Flop u_Q0 (.clk(clock_1_out), .D(blackboxromsimplified_1_q0new), .Q(Q0));  // open: Qn, preset, en, reset
  D_Flip_Flop u_Q1 (.clk(clock_1_out), .D(blackboxromsimplified_1_q1new), .Q(Q1));  // open: Qn, preset, en, reset
endmodule

module BlackBoxRomSimplified (
  input  Q0,
  input  Q1,
  output Q0new,
  output Q1new
);

  ROM #(.addrWidth(2), .dataWidth(2)) rom_1 (.addr({Q1, Q0}), .data({Q1new, Q0new}));  // open: sel

  // Notes on the sheet:
  //   contents of rom_1 (hex, n*v repeats v):
  //   1 2 3
endmodule
