// Logisim project mod4-counter-ROM.circ as structural Verilog: 2 circuits, main circuit main
module main (
  output Q1,
  output Q0
);

  wire blackboxrom_1_q0new, blackboxrom_1_q1new, clock_1_out;

  Clock clock_1 (.out(clock_1_out));
  BlackBoxROM blackboxrom_1 (
    .Q0(Q0), .Q1(Q1), .C(clock_1_out), .Q0new(blackboxrom_1_q0new), .Q1new(blackboxrom_1_q1new));
  D_Flip_Flop u_Q0 (.clk(clock_1_out), .D(blackboxrom_1_q0new), .Q(Q0));  // open: Qn, preset, en, reset
  D_Flip_Flop u_Q1 (.clk(clock_1_out), .D(blackboxrom_1_q1new), .Q(Q1));  // open: Qn, preset, en, reset
endmodule

module BlackBoxROM (
  input  Q0,
  input  Q1,
  input  C,
  output Q0new,
  output Q1new
);

  wire [2:2] not_1_out;

  not not_1 (not_1_out[2], C);
  ROM #(.addrWidth(3), .dataWidth(2)) rom_1 (.addr({not_1_out[2], Q1, Q0}), .data({Q1new, Q0new}));  // open: sel

  // Notes on the sheet:
  //   contents of rom_1 (hex, n*v repeats v):
  //   0 3 0 3 1 2 3
endmodule
