// Logisim project mod4-counter.circ as structural Verilog: 2 circuits, main circuit main
module main (
  output Q1,
  output Q0
);

  wire blackbox_1_q0new, blackbox_1_q1new, clock_1_out;

  Clock clock_1 (.out(clock_1_out));
  BlackBox blackbox_1 (.Q0(Q0), .Q1(Q1), .C(clock_1_out), .Q0new(blackbox_1_q0new), .Q1new(blackbox_1_q1new));
  D_Flip_Flop u_Q0 (.clk(clock_1_out), .D(blackbox_1_q0new), .Q(Q0));  // open: Qn, preset, en, reset
  D_Flip_Flop u_Q1 (.clk(clock_1_out), .D(blackbox_1_q1new), .Q(Q1));  // open: Qn, preset, en, reset
endmodule

module BlackBox (
  input  Q0,
  input  Q1,
  input  C,
  output Q0new,
  output Q1new
);

  wire and_1_out, and_2_out, and_3_out, and_4_out, and_5_out, not_1_out, not_2_out, not_3_out, not_4_out;

  not not_1 (not_1_out, Q0);
  not not_2 (not_2_out, C);
  not not_3 (not_3_out, Q1);
  not not_4 (not_4_out, not_2_out);
  and and_1 (and_1_out, Q0, not_4_out);
  and and_2 (and_2_out, not_1_out, not_2_out);
  and and_3 (and_3_out, Q0, not_3_out);
  and and_4 (and_4_out, Q0, not_4_out);
  and and_5 (and_5_out, not_1_out, Q1, not_2_out);
  or or_1 (Q0new, and_1_out, and_2_out);
  or or_2 (Q1new, and_3_out, and_4_out, and_5_out);
endmodule
