// Logisim project finalCircuit.circ as structural Verilog: 1 circuit, main circuit main
module main (
  input  A,
  input  B,
  output A_prime_B_prime_AB
);

  wire and_1_out, and_2_out, not_1_out, not_2_out;

  not not_1 (not_1_out, A);
  not not_2 (not_2_out, B);
  and and_1 (and_1_out, B, A);
  and and_2 (and_2_out, not_1_out, not_2_out);
  or or_1 (A_prime_B_prime_AB, and_1_out, and_2_out);

  // Notes on the sheet:
  //   AB
  //   A'B'
  //   Nick Hinke
endmodule
